# Fritzing sketch hbridge_basic (saved by Fritzing 0.9.3b)

parts:
  R1 = Resistor [tolerance=±5% resistance=1k package=THT]
  R2 = Resistor [tolerance=±5% resistance=1k package=THT]
  IN = female pin header, 2 pins [form="♀ (female)"]
  R3 = Resistor [tolerance=±5% resistance=1k package=THT]
  R4 = Resistor [tolerance=±5% resistance=1k package=THT]
  Q2 = TIP120 Hi-Current Darlington Transistor
  D1 = Rectifier Diode [part_number=1N4001 package="300 mil [THT]"]
  Q3 = TIP120 Hi-Current Darlington Transistor
  D2 = Rectifier Diode [part_number=1N4001 package="300 mil [THT]"]
  Q4 = TIP120 Hi-Current Darlington Transistor
  D3 = Rectifier Diode [part_number=1N4001 package="300 mil [THT]"]
  Q5 = TIP120 Hi-Current Darlington Transistor
  D4 = Rectifier Diode [part_number=1N4001 package="300 mil [THT]"]
  Attiny85 = attiny85 [package=dip]
  OUT = female pin header, 2 pins [form="♀ (female)"]
  R5 = Resistor [tolerance=±5% resistance=1k package=THT]
  R6 = Resistor [tolerance=±5% resistance=1k package=THT]
  R7 = Resistor [tolerance=±5% resistance=1k package=THT]
  R8 = Resistor [tolerance=±5% resistance=1k package=THT]
  OUT1 = female pin header, 2 pins [form="♀ (female)"]
  IN1 = female pin header, 2 pins [form="♀ (female)"]
  Q6 = TIP120 Hi-Current Darlington Transistor
  Q7 = TIP120 Hi-Current Darlington Transistor
  Attiny86 = attiny85 [package=dip]
  Q8 = TIP120 Hi-Current Darlington Transistor
  Q9 = TIP120 Hi-Current Darlington Transistor
  D5 = Rectifier Diode [part_number=1N4001 package="300 mil [THT]"]
  D6 = Rectifier Diode [part_number=1N4001 package="300 mil [THT]"]
  D7 = Rectifier Diode [part_number=1N4001 package="300 mil [THT]"]
  D8 = Rectifier Diode [part_number=1N4001 package="300 mil [THT]"]

nets:
  N1: R1.Pin_0, R2.Pin_0, IN.pin2, Attiny85.Pin_5
  N2: R1.Pin_1, Q3.BASE
  N3: R2.Pin_1, Q2.BASE
  N4: IN.pin1, R3.Pin_0, R4.Pin_0, Attiny85.Pin_6
  N5: R3.Pin_1, Q5.BASE
  N6: R4.Pin_1, Q4.BASE
  N7: Q2.COLLECTOR, D1.cathode, Q5.COLLECTOR, D4.cathode, Attiny85.Pin_8
  N8: Q2.EMITTER, D1.anode, Q4.COLLECTOR, D3.cathode, OUT.pin2
  N9: Q3.COLLECTOR, D2.cathode, Q5.EMITTER, D4.anode, OUT.pin1
  N10: Q3.EMITTER, D2.anode, Q4.EMITTER, D3.anode, Attiny85.Pin_4
  N11: R5.Pin_0, R6.Pin_0, IN1.pin1, Attiny86.Pin_6
  N12: R5.Pin_1, Q7.BASE
  N13: R6.Pin_1, Q6.BASE
  N14: R7.Pin_0, R8.Pin_0, IN1.pin2, Attiny86.Pin_5
  N15: R7.Pin_1, Q9.BASE
  N16: R8.Pin_1, Q8.BASE
  N17: OUT1.pin1, Q7.EMITTER, Q8.COLLECTOR, D6.anode, D8.cathode
  N18: OUT1.pin2, Q6.COLLECTOR, Q9.EMITTER, D5.anode, D7.cathode
  N19: Q6.EMITTER, Attiny86.Pin_4, Q8.EMITTER, D7.anode, D8.anode
  N20: Q7.COLLECTOR, Attiny86.Pin_8, Q9.COLLECTOR, D5.cathode, D6.cathode
